# Fritzing sketch session2-version2 (saved by Fritzing 0.9.2b)
circuit board: 10cm x 15cm
breadboards: 1

parts:
  LCD_Screen = LCD screen
  Switch = Pushbutton [package="[THT]"]
  Switch_2 = Pushbutton [package="[THT]"]
  Switch_3 = Pushbutton [package="[THT]"]
  LRD = Photocell (LDR) [package=THT]
  LRD_2 = Photocell (LDR) [package=THT]
  LRD_3 = Photocell (LDR) [package=THT]
  10k = Resistor [tolerance=±5% resistance=10k package=THT]
  10k_2 = Resistor [tolerance=±5% resistance=10k package=THT]
  10k_3 = Resistor [tolerance=±5% resistance=10k package=THT]
  10k_4 = Resistor [tolerance=±5% resistance=10k package=THT]
  10k_5 = Resistor [tolerance=±5% resistance=0 package=THT]
  10k_6 = Resistor [tolerance=±5% resistance=10k package=THT]
  10k_7 = Resistor [tolerance=±5% resistance=10k package=THT]
  1k_Resistor = Resistor [tolerance=±5% resistance=1k package=THT]
  10K_Potentiometer = Rotary Potentiometer (Large) [maximum_resistance=10kΩ package=THT]
  Switch_4 = Pushbutton [package="[THT]"]
  RGB_LED = RGB LED - (4 legs) [package="5 mm [THT]"]
  + = Piezo Speaker
  Speaker = female pin header, 4 pins [form="♀ (female)"]
  J1 = female pin header, 5 pins [form="♀ (female)"]  # not connected
  ARDUINO = Arduino Uno (Rev3)

nets:
  VSS: LCD_Screen.VSS, LCD_Screen.R/W, LCD_Screen.LED-, 10k.Pin_0, 10k_2.Pin_0, 10k_3.Pin_0, 10k_4.Pin_0, 10k_5.Pin_0, 10k_6.Pin_0, 10k_7.Pin_0, 1k_Resistor.Pin_1, 10K_Potentiometer.leg1, +.pin1, ARDUINO.GND
  VDD: LCD_Screen.VDD, LCD_Screen.LED+, Switch.Pin_3, Switch.Pin_4, Switch_2.Pin_3, Switch_2.Pin_4, Switch_3.Pin_3, Switch_3.Pin_4, LRD.pin_0, LRD_2.pin_0, LRD_3.pin_0, 10K_Potentiometer.leg2, Switch_4.Pin_3, Switch_4.Pin_4, RGB_LED.common_anode, ARDUINO.5V
  N1: LCD_Screen.V0, 1k_Resistor.Pin_0
  N2: LCD_Screen.RS, ARDUINO.D2
  N3: LCD_Screen.E, ARDUINO.D3_PWM
  N4: LCD_Screen.DB4, ARDUINO.D4
  N5: LCD_Screen.DB5, ARDUINO.D5_PWM
  N6: LCD_Screen.DB6, ARDUINO.D6_PWM
  N7: LCD_Screen.DB7, ARDUINO.D7
  N8: Switch.Pin_1, Switch.Pin_2, 10k_2.Pin_1, ARDUINO.D13/SCK
  N9: Switch_2.Pin_1, Switch_2.Pin_2, 10k_3.Pin_1, ARDUINO.D12/MISO
  N10: Switch_3.Pin_1, Switch_3.Pin_2, 10k_4.Pin_1, ARDUINO.A4/SDA
  N11: LRD.pin_1, 10k_6.Pin_1, ARDUINO.A0
  N12: LRD_2.pin_1, 10k.Pin_1, ARDUINO.A1
  N13: LRD_3.pin_1, 10k_7.Pin_1, ARDUINO.A2
  N14: 10k_5.Pin_1, Switch_4.Pin_1, Switch_4.Pin_2, ARDUINO.A5/SCL
  N15: 10K_Potentiometer.wiper, ARDUINO.A3
  N16: RGB_LED.red_cathode, ARDUINO.D9_PWM
  N17: RGB_LED.green_cathode, ARDUINO.D10_PWM/SS
  N18: RGB_LED.blue_cathode, ARDUINO.D11_PWM/MOSI
  N19: +.pin2, ARDUINO.D8
  N20: Speaker.pin1, Speaker.pin3

notes:
  http://morgan.isnot.in/CMHK/ElectronicsWorkshop/
